# Fritzing sketch Antifumo-Ethernet (saved by Fritzing 0.9.3b)

parts:
  Componente1 = MQ-7 breakout
  Componente2 = Arduino Uno (Rev3)  # not connected
  Componente3 = Arduino Ethernet Shield (Rev3)

nets:
  VCC: Componente1.VCC, Componente3.5V
  GND: Componente1.GND, Componente3.GND
  N1: Componente1.AO, Componente3.A0

notes:
  SIMORIA 1P2, SIstema de MOnitorización y RIego Automático., 1

custom parts:
  MQ-7 breakout: SKU: 101282
