# Fritzing sketch dallas (saved by Fritzing 0.9.3b)
breadboards: 1

parts:
  Componente1 = Arduino Uno (Rev3)
  U3 = Nokia 6100 Color LCD [package=nokia6100_lcd]
  Part1 = KY-001 Temperature Sensor Module [package="Breakout board"]

nets:
  N1: Componente1.GND, U3.VDISPLAY, Part1.-
  N2: Componente1.D0/RX, U3.LEDGND
  N3: Componente1.D1/TX, U3.GND
  N4: Componente1.D2, Part1.S
  5V: Componente1.5V, U3.VLED, Part1.Vin

custom parts:
  KY-001 Temperature Sensor Module: Arduino Temperature Sensor Module Keyes KY-001, Allows ambient temperature measurement using digital serial bus (DS18B20)
