# Fritzing sketch dht (saved by Fritzing 0.9.3b)
breadboards: 1

parts:
  Componente1 = Arduino Uno (Rev3)
  DHT1 = DHT11 Humitidy and Temperature Sensor
  U3 = Nokia 6100 Color LCD [package=nokia6100_lcd]

nets:
  N1: Componente1.D12/MISO, DHT1.DATA
  GND: Componente1.GND, DHT1.GND, U3.VDISPLAY
  N2: Componente1.D0/RX, U3.LEDGND
  N3: Componente1.D1/TX, U3.GND
  3V3: Componente1.3V3, DHT1.VDD
  N4: Componente1.5V, U3.VLED

custom parts:
  DHT11 Humitidy and Temperature Sensor: DHT11 Humidity and Temperature Sensor
