# Fritzing sketch Serra domotizzata (saved by Fritzing 0.9.3b)
breadboards: 1

parts:
  Fotoresistenza = PHOTOCELL [package=photocell]
  DHT11_(_Temperatura_e_umidità) = DHT11 Humitidy and Temperature Sensor
  Modulo_4_Relè = OPENMolo 4 Relay breakout board
  Sensore_Livello_Acqua = Water Level Sensor
  J1 = Piezo Speaker
  10K_OHM = Resistor [tolerance=±5% resistance=10k package="0805 [SMD]"]
  LED1 = LED - 5mm [color="Red (633nm)" package="5 mm [THT]"]
  R1 = Resistor [tolerance=±5% resistance=220 package=THT]
  DC-DC_12V-5V = DC-DC Power Module (5v)
  Sensore_Umidità_suolo = DFRobot Capacitive Soil Moisture Sensor V1.0 [part_number=SEN0193]
  U4 = Nokia 6100 Color LCD [package=nokia6100_lcd]
  Componente1 = Arduino Uno (Rev3)

nets:
  GND: Fotoresistenza.P$1, DHT11_(_Temperatura_e_umidità).GND, Modulo_4_Relè.GND, J1.pin1, LED1.cathode, DC-DC_12V-5V.GND*, Sensore_Umidità_suolo.GND, U4.VDISPLAY
  N1: Fotoresistenza.P$2, 10K_OHM.Pin_0, Componente1.A0
  VCC: DHT11_(_Temperatura_e_umidità).VDD, Modulo_4_Relè.VCC, Sensore_Livello_Acqua.VCC, 10K_OHM.Pin_1, DC-DC_12V-5V.Vout, Sensore_Umidità_suolo.VCC, U4.VLED
  N2: DHT11_(_Temperatura_e_umidità).DATA, Componente1.D12/MISO
  N3: Modulo_4_Relè.E3, Componente1.D11_PWM/MOSI
  N4: Modulo_4_Relè.E2, Componente1.D10_PWM/SS
  N5: Modulo_4_Relè.E1, Componente1.D9_PWM
  N6: Sensore_Livello_Acqua.SIG, Componente1.A1
  N7: J1.pin2, Componente1.D3_PWM
  N8: LED1.anode, R1.Pin_0
  N9: R1.Pin_1, Componente1.D13/SCK
  N10: Sensore_Umidità_suolo.A, Componente1.A3
  N11: U4.GND, Componente1.D1/TX
  N12: U4.LEDGND, Componente1.D0/RX

notes:
  AC-DC Power 240V-12V

custom parts:
  DHT11 Humitidy and Temperature Sensor: DHT11 Humidity and Temperature Sensor
  OPENMolo 4 Relay breakout board: Módulo de 8 relés de 10A optoaislados pensado para desarrollos rápidos basadon en microcontroladores o microcomputadoras. Estos módulos son diseñados con especial cuidado tanto en sus capacidades aisladoras para preservar equipos de mayor valor asi como en las fijaciones para evitar problemas a la hora de armar un prototipo o de fijarlo en un tablero definitivo. Una importante característica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
  Water Level Sensor: A water level sensor. This sensor operates at 3V to 5V. The Sig (signal) pin outputs an analogue signal that is in proportion to the amount of water in contact with the sensor.
  DC-DC Power Module (5v): DC-DC Power Module based con AMS1117-5.0 Input: DC 6~12V (input power must higher 1V than output power); Output: 5V (+/-0.05V error), 800mA
  DFRobot Capacitive Soil Moisture Sensor V1.0: DFRobot Capacitive Soil Moisture Sensor V1.0 This product measures soil moisture levels by capacitive sensing, rather than resistive sensing like other types of moisture sensor. It is made of a corrosion resistant material giving it a long service life. Insert it into soil and impress your friends with the real-time soil moisture data! The product includes an on-board voltage regulator which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
